# Fritzing sketch Diagram (saved by Fritzing 0.9.3b)
breadboards: 1

parts:
  Componente1 = Arduino Mega ADK (Rev3)
  U1 = ESP8266 NodeMCU LoLin module
  DHT1 = Humidity and Temperature Sensor DHT11
  Componente2 = Triple Axis Accelerometer Breakout - ADXL335
  Componente3 = Breakout Board for Electret Microphone
  R2 = Photocell (LDR) [package=THT]
  R3 = Resistor [tolerance=±5% resistance=300 package="1206 [SMD]"]
  YL-83_-_Detection_Board1 = YL-83 Rain Sensor - Detection Board
  YL-83_-_Control_Board1 = YL-83 Rain Sensor - Control Board
  Componente4 = MQ-4
  LED1 = RGB LED (com. cathode, rgb) [package="5 mm [THT]"]
  R4 = Resistor [tolerance=±5% resistance=220 package=THT]
  R5 = Resistor [tolerance=±5% resistance=220 package=THT]
  R6 = Resistor [tolerance=±5% resistance=220 package=THT]
  R7 = Rotary Potentiometer (Small) [maximum_resistance=100kΩ package=THT]

nets:
  N1: Componente1.A0, R3.Pin_0
  N2: Componente1.A1, Componente2.ZOUT
  N3: Componente1.A2, Componente2.YOUT
  N4: Componente1.A3, Componente2.XOUT
  N5: Componente1.A4, Componente3.AUD
  N6: Componente1.A5, YL-83_-_Control_Board1.AO
  N7: Componente1.A6, Componente4.AO
  N8: Componente1.A7, R7.wiper
  GND: Componente1.GND, DHT1.GND_1, Componente2.GND, Componente3.GND, R2.pin_0, R3.Pin_1, YL-83_-_Control_Board1.GND, Componente4.GND, LED1.common_cathode, R7.leg1
  N9: Componente1.D10_PWM, R6.Pin_0
  N10: Componente1.D9_PWM, R5.Pin_0
  N11: Componente1.D8_PWM, R4.Pin_0
  VCC: Componente1.VIN, DHT1.Vcc, Componente2.VCC, Componente3.VCC, R2.pin_1, YL-83_-_Control_Board1.VCC, Componente4.VCC, R7.leg2
  N12: Componente1.D0/RX0, U1.TX
  N13: Componente1.D1/TX0, U1.RX
  N14: Componente1.D5_PWM, DHT1.Data-signal
  N15: YL-83_-_Detection_Board1.POS, YL-83_-_Control_Board1.POS
  N16: YL-83_-_Detection_Board1.NEG, YL-83_-_Control_Board1.NEG
  N17: LED1.red_anode, R6.Pin_1
  N18: LED1.green_anode, R5.Pin_1
  N19: LED1.blue_anode, R4.Pin_1

custom parts:
  ESP8266 NodeMCU LoLin module: ESP8266 based NodeMCU
  Humidity and Temperature Sensor DHT11: Digital relative humidity & temperature sensor DHT11
  YL-83 Rain Sensor - Detection Board: The YL-83 is a rain sensor that has more resistance when dry and less resistance when wet. The module runs at 5V.
  YL-83 Rain Sensor - Control Board: The YL-83 is a rain sensor that has more resistance when dry and less resistance when wet. The module runs at 5V.
